# Fritzing sketch Les-1-Fritzing (saved by Fritzing 0.9.4)
breadboards: 1

parts:
  Part1 = Arduino Uno (Rev3)
  LED1 = LED - 5mm [color="Red (633nm)" package="5 mm [THT]"]
  Part2 = Arduino Uno (Rev3)
  S1 = Toggle Switch [package=THT]
  R1 = Resistor [tolerance=±5% resistance=220 package=THT]  # not connected
  S2 = Pushbutton [package="[THT]"]  # not connected

nets:
  N1: Part1.A4/SDA, Part2.A4/SDA
  N2: Part1.A5/SCL, Part2.A5/SCL
  N3: Part1.D7, S1.COM
  GND: Part1.GND, LED1.anode, Part2.GND
  N4: LED1.cathode, Part2.AREF
